// Logisim project conversor2.circ as structural Verilog: 1 circuit, main circuit main
// 4
module main (
);

  wire and_1_out, and_2_out, and_3_out, and_4_out, and_5_out, and_6_out, and_7_out, and_8_out, and_9_out,
       and_10_out, and_11_out, or_1_out, or_2_out, xor_3_out, xor_4_out, xor_5_out, xor_6_out, xor_7_out,
       xor_8_out, xor_10_out, xor_11_out, xor_14_out;
  wire [2:0] xor_1_out, xor_2_out, xor_13_out, xor_16_out;
  wire [2:2] xor_15_out;
  wire [3:1] xor_17_out;

  assign xor_1_out = 3'b110 ^ 3'b111;  // XOR_Gate xor_1, 3 bits wide
  assign xor_2_out = 3'b010 ^ 3'b000;  // XOR_Gate xor_2, 3 bits wide
  xor xor_3 (xor_3_out, 1'b1, xor_1_out[2]);
  and and_1 (and_1_out, 1'b1, xor_1_out[2]);
  xor xor_4 (xor_4_out, and_1_out, xor_1_out[1]);
  and and_2 (and_2_out, and_1_out, xor_1_out[1]);
  xor xor_5 (xor_5_out, and_2_out, xor_1_out[0]);
  xor xor_6 (xor_6_out, 1'b0, xor_2_out[2]);
  and and_3 (and_3_out, 1'b0, xor_2_out[2]);
  xor xor_7 (xor_7_out, and_3_out, xor_2_out[1]);
  and and_4 (and_4_out, and_3_out, xor_2_out[1]);
  xor xor_8 (xor_8_out, and_4_out, xor_2_out[0]);
  xor xor_9 (xor_13_out[2], xor_3_out, xor_6_out);
  and and_5 (and_5_out, xor_3_out, xor_6_out);
  xor xor_10 (xor_10_out, xor_4_out, xor_7_out);
  and and_6 (and_6_out, xor_4_out, xor_7_out);
  xor xor_11 (xor_11_out, xor_5_out, xor_8_out);
  and and_7 (and_7_out, xor_5_out, xor_8_out);
  xor xor_12 (xor_13_out[1], and_5_out, xor_10_out);
  and and_8 (and_8_out, and_5_out, xor_10_out);
  xor xor_13 (xor_13_out[0], or_1_out, xor_11_out);
  and and_9 (and_9_out, or_1_out, xor_11_out);
  xor xor_14 (xor_14_out, 1'b1, 1'b0);
  or or_1 (or_1_out, and_8_out, and_6_out);
  or or_2 (or_2_out, and_9_out, and_7_out);
  xor xor_15 (xor_15_out[2], or_2_out, xor_14_out);
  assign xor_16_out = xor_13_out ^ {3{xor_15_out[2]}};  // XOR_Gate xor_16, 3 bits wide
  xor xor_17 (xor_17_out[3], xor_16_out[2], and_10_out);
  and and_10 (and_10_out, xor_16_out[1], and_11_out);
  xor xor_18 (xor_17_out[2], xor_16_out[1], and_11_out);
  and and_11 (and_11_out, xor_16_out[0], xor_15_out[2]);
  xor xor_19 (xor_17_out[1], xor_16_out[0], xor_15_out[2]);
  LED led_1 (.in(xor_17_out[1]));
  LED led_2 (.in(xor_17_out[2]));
  LED led_3 (.in(xor_15_out[2]));
  Hex_Digit_Display hex_digit_display_1 (.value({1'b0, xor_17_out[1], xor_17_out[2], xor_17_out[3]}));  // open: dp
  LED led_4 (.in(xor_15_out[2]));
  LED led_5 (.in(xor_17_out[3]));
endmodule
