// Logisim project somador-subtrator-final.circ as structural Verilog: 1 circuit, main circuit main
module main (
);

  wire and_1_out, and_2_out, and_3_out, and_4_out, and_5_out, and_6_out, and_7_out, and_8_out, or_1_out,
       or_2_out, or_3_out, or_4_out, xor_2_out, xor_4_out, xor_5_out, xor_7_out;
  wire [3:0] xor_1_out, xor_3_out;

  Hex_Digit_Display hex_digit_display_1 (.value(4'b0010));  // open: dp
  Hex_Digit_Display hex_digit_display_2 (.value(4'b0100));  // open: dp
  assign xor_1_out = 4'b1111 ^ 4'b0010;  // XOR_Gate xor_1, 4 bits wide
  xor xor_2 (xor_2_out, xor_1_out[0], 1'b0);
  and and_1 (and_1_out, xor_1_out[0], 1'b0);
  xor xor_3 (xor_3_out[0], 1'b1, xor_2_out);
  and and_2 (and_2_out, 1'b1, xor_2_out);
  xor xor_4 (xor_4_out, xor_1_out[1], 1'b0);
  and and_3 (and_3_out, xor_1_out[1], 1'b0);
  xor xor_5 (xor_5_out, xor_1_out[2], 1'b1);
  and and_4 (and_4_out, xor_1_out[2], 1'b1);
  or or_1 (or_1_out, and_2_out, and_1_out);
  xor xor_6 (xor_3_out[1], or_1_out, xor_4_out);
  and and_5 (and_5_out, or_1_out, xor_4_out);
  xor xor_7 (xor_7_out, xor_1_out[3], 1'b0);
  and and_6 (and_6_out, xor_1_out[3], 1'b0);
  or or_2 (or_2_out, and_5_out, and_3_out);
  xor xor_8 (xor_3_out[2], or_2_out, xor_5_out);
  and and_7 (and_7_out, or_2_out, xor_5_out);
  or or_3 (or_3_out, and_7_out, and_4_out);
  xor xor_9 (xor_3_out[3], or_3_out, xor_7_out);
  and and_8 (and_8_out, or_3_out, xor_7_out);
  or or_4 (or_4_out, and_8_out, and_6_out);
  LED led_1 (.in(or_4_out));
  LED led_2 (.in(xor_3_out[3]));
  Hex_Digit_Display hex_digit_display_3 (.value(xor_3_out));  // open: dp
  LED led_3 (.in(xor_3_out[2]));
  LED led_4 (.in(xor_3_out[1]));
  Hex_Digit_Display hex_digit_display_4 (.value({1'b0, xor_3_out[2:0]}));  // open: dp
  LED led_5 (.in(xor_3_out[3]));
  LED led_6 (.in(xor_3_out[0]));

  // Notes on the sheet:
  //   Carry in. 0 soma, 1 subtrai.
  //   operando B
  //   operando A
  //   Carry out
  //   Resultado
endmodule
